// Logisim project COMBINATION NAND.circ as structural Verilog: 2 circuits, main circuit main
module main (
  input  A,
  input  B,
  input  C,
  output out_4
);

  wire nand_1_out_9, nand_1_out_10, nand_1_out_11, nand_1_out_12, nand_2_out_11, nand_3_out_9, nand_3_out_11;

  NAND nand_1 (
    .in_1(B), .in_2(nand_1_out_9), .in_3(nand_2_out_11), .in_4(nand_1_out_9), .in_5(A), .in_6(nand_1_out_11),
    .in_7(C), .in_8(nand_1_out_11), .out_9(nand_1_out_9), .out_10(nand_1_out_10), .out_11(nand_1_out_11),
    .out_12(nand_1_out_12));
  NAND nand_2 (
    .in_5(C), .in_7(C), .out_11(nand_2_out_11));  // open: in_1, in_2, in_3, in_4, in_6, in_8, out_9, out_10, out_12
  NAND nand_3 (
    .in_1(nand_1_out_10), .in_2(nand_3_out_9), .in_3(nand_1_out_10), .in_4(nand_3_out_11),
    .in_5(nand_1_out_12), .in_7(nand_1_out_12), .out_9(nand_3_out_9), .out_10(out_4), .out_11(nand_3_out_11));  // open: in_6, in_8, out_12
endmodule

module NAND (
  input  in_1,
  input  in_2,
  input  in_3,
  input  in_4,
  input  in_5,
  input  in_6,
  input  in_7,
  input  in_8,
  output out_9,
  output out_10,
  output out_11,
  output out_12
);

  nand nand_1 (out_9, in_1, in_3);
  nand nand_2 (out_11, in_5, in_7);
  nand nand_3 (out_10, in_2, in_4);
  nand nand_4 (out_12, in_6, in_8);
endmodule
