// Logisim project COMBINATION NOR.circ as structural Verilog: 2 circuits, main circuit main
module main (
  input  A,
  input  B,
  input  C,
  output out_4
);

  wire nor_1_out_9, nor_1_out_10, nor_1_out_11, nor_1_out_12, nor_2_out_9, nor_3_out_9, nor_3_out_10,
       nor_3_out_11;

  NOR nor_1 (
    .in_1(A), .in_2(C), .in_3(A), .in_4(C), .in_5(nor_1_out_9), .in_6(C), .in_7(nor_1_out_10), .in_8(C),
    .out_9(nor_1_out_9), .out_10(nor_1_out_10), .out_11(nor_1_out_11), .out_12(nor_1_out_12));
  NOR nor_2 (
    .in_1(nor_1_out_11), .in_3(nor_3_out_11), .in_5(nor_2_out_9), .in_7(nor_2_out_9), .out_9(nor_2_out_9),
    .out_11(out_4));  // open: in_2, in_4, in_6, in_8, out_10, out_12
  NOR nor_3 (
    .in_1(B), .in_2(nor_1_out_12), .in_3(B), .in_4(nor_1_out_12), .in_5(nor_3_out_9), .in_7(nor_3_out_10),
    .out_9(nor_3_out_9), .out_10(nor_3_out_10), .out_11(nor_3_out_11));  // open: in_6, in_8, out_12
endmodule

module NOR (
  input  in_1,
  input  in_2,
  input  in_3,
  input  in_4,
  input  in_5,
  input  in_6,
  input  in_7,
  input  in_8,
  output out_9,
  output out_10,
  output out_11,
  output out_12
);

  nor nor_1 (out_9, in_1, in_3);
  nor nor_2 (out_11, in_5, in_7);
  nor nor_3 (out_10, in_2, in_4);
  nor nor_4 (out_12, in_6, in_8);
endmodule
