// Logisim project NAND as a universal gate.circ as structural Verilog: 1 circuit, main circuit main
module main (
  input  A,
  input  A_2,
  input  B,
  input  A_3,
  input  B_2,
  output A_A__prime_A_prime,
  output AB,
  output A_prime_B_prime__prime_A_B
);

  wire nand_2_out, nand_3_out, nand_4_out;

  nand nand_1 (A_A__prime_A_prime, A, A);
  nand nand_2 (nand_2_out, A_2, B);
  nand nand_3 (nand_3_out, A_3, A_3);
  nand nand_4 (nand_4_out, B_2, B_2);
  nand nand_5 (AB, nand_2_out, nand_2_out);
  nand nand_6 (A_prime_B_prime__prime_A_B, nand_3_out, nand_4_out);

  // Notes on the sheet:
  //   (AB)'
endmodule
