// Logisim project NOR gate as a universal gate.circ as structural Verilog: 1 circuit, main circuit main
module main (
  input  A,
  input  A_2,
  input  B,
  input  A_3,
  input  B_2,
  output A_A__prime_A_prime,
  output A_prime_B_prime__prime_AB,
  output A_B
);

  wire nor_1_out, nor_2_out, nor_3_out;

  nor nor_1 (nor_1_out, A_2, A_2);
  nor nor_2 (nor_2_out, B, B);
  nor nor_3 (nor_3_out, A_3, B_2);
  nor nor_4 (A_A__prime_A_prime, A, A);
  nor nor_5 (A_prime_B_prime__prime_AB, nor_1_out, nor_2_out);
  nor nor_6 (A_B, nor_3_out, nor_3_out);

  // Notes on the sheet:
  //   A'
  //   B'
  //   (A+B)'
endmodule
