// Logisim project XOR using NAND.circ as structural Verilog: 1 circuit, main circuit main
// A
module main (
  input  A,
  input  B,
  output A_prime_AB___B_prime_AB
);

  wire nand_1_out, nand_2_out, nand_3_out;

  nand nand_1 (nand_1_out, A, B);
  nand nand_2 (nand_2_out, A, nand_1_out);
  nand nand_3 (nand_3_out, nand_1_out, B);
  nand nand_4 (A_prime_AB___B_prime_AB, nand_2_out, nand_3_out);

  // Notes on the sheet:
  //   AB'
  //   (A.(AB)')' = A' + AB
  //   B.AB'=B'+AB
endmodule
